# Fritzing sketch skema (saved by Fritzing 0.9.3b)

parts:
  A1 = Raspberry Pi 5
  U1 = LM2596 step down module
  Part1 = Adafruit ADS1115 16Bit I2C ADC [part_number="Adafruit #1085"]
  J1 = Basic Servo
  M1 = Stepper Motor - Bipolar
  J2 = Basic Servo
  e-radionica_com1 = LM393 LDR breakout [part_number=100027]
  U3 = Luxeon LED [package=luxeon]
  J3 = Infrared Proximity Sensor
  Q1 = NPN-Transistor [package="SOT-23 [SMD]"]
  Part2 = Adafruit TB6612 DC and Stepper Motor Driver [part_number="Adafruit #2448"]
  PWM1 = PCA9685 16x12-bit PWM Breakout

nets:
  3V3: A1.3V3, Part1.VDD, e-radionica_com1.VCC
  N1: A1.GPIO2, Part1.SDA, PWM1.no_name_yet#503
  N2: A1.GPIO3, Part1.SCL, PWM1.no_name_yet#504
  GND: A1.GND, A1.Fan-GND, U1.IN-, U1.OUT-, Part1.ADDR, Part1.GND, J1.gnd, J2.gnd, J3.GND, PWM1.no_name_yet#501, PWM1.no_name_yet#701
  N3: A1.GPIO16, Part2.BIN2
  N4: A1.GPIO26, Part2.PWMB
  N5: A1.GPIO20, J3.Vout
  N6: A1.GPIO21, Q1.0
  N7: U1.OUT+, J3.Vcc, Q1.2, PWM1.no_name_yet#505, PWM1.no_name_yet#605
  N8: Part1.AIN0, e-radionica_com1.AO
  VCC: J1.vcc, J2.vcc, PWM1.no_name_yet#706
  N9: J1.pulse, PWM1.no_name_yet#1
  N10: M1.A, Part2.MOTORB2
  N11: M1.C, Part2.MOTORB1
  N12: M1.B, Part2.MOTORA2
  N13: M1.D, Part2.MOTORA1
  N14: J2.pulse, PWM1.no_name_yet#0
  GND_2: e-radionica_com1.GND, U3.C, Part2.GND
  N15: U3.A, Q1.1

custom parts:
  Raspberry Pi 5: The RPi5, a faster version of the awesome Raspberry Pi4B ARM Board with 40 pin gpio.
  LM2596 step down module: LM2596 DC-DC step down power supply module 3 A.
  Adafruit ADS1115 16Bit I2C ADC: For microcontrollers without an analog-to-digital converter or when you want a higher-precision ADC, the ADS1115 provides 16-bit precision at 860 samples/second over I2C. The chip can be configured as 4 single-ended input channels, or two differential channels. As a nice bonus, it even includes a programmable gain amplifier, up to x16, to help boost up smaller single/differential signals to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
  Adafruit TB6612 DC and Stepper Motor Driver: Spin two DC motors, step one bi-polar or uni-polar stepper, or fire off two solenoids with 1.2A per channel using the TB6612. These are perhaps better known as "the drivers in our assembled Adafruit Motorshield or Motor HAT." We really like these dual H-bridges, so if you want to control motors without a shield or HAT these are easy to include on any solderless breadboard or perma-proto.
